// Logisim project whole_circuit_cylrx.circ as structural Verilog: 1 circuit, main circuit main
module main (
);

  wire and_1_out, and_2_out, and_3_out, and_4_out, and_5_out, and_6_out, and_7_out, button_1_out,
       button_2_out, button_3_out, button_4_out, button_5_out, button_6_out, button_7_out, button_8_out,
       not_1_out, not_2_out, not_3_out, not_4_out, not_5_out, or_1_out, S2_out, S3_out, S4_out, S5_out,
       S6_out, S7_out;
  wire [2:0] priority_encoder_1_out;

  Button button_1 (.out(button_1_out));
  Button button_2 (.out(button_2_out));
  Button button_3 (.out(button_3_out));
  Button button_4 (.out(button_4_out));
  Button button_5 (.out(button_5_out));
  Button button_6 (.out(button_6_out));
  Button button_7 (.out(button_7_out));
  Button button_8 (.out(button_8_out));
  Priority_Encoder priority_encoder_1 (
    .in0(button_1_out), .in1(button_2_out), .in2(button_3_out), .in3(button_4_out), .in4(button_5_out),
    .in5(button_6_out), .in6(button_7_out), .in7(button_8_out), .out(priority_encoder_1_out));  // open: en_in, gs, en_out
  not not_1 (not_1_out, priority_encoder_1_out[2]);
  not not_2 (not_2_out, priority_encoder_1_out[1]);
  not not_3 (not_3_out, priority_encoder_1_out[0]);
  not not_4 (not_4_out, priority_encoder_1_out[2]);
  not not_5 (not_5_out, priority_encoder_1_out[0]);
  and and_1 (and_1_out, priority_encoder_1_out[2], not_2_out);
  and and_2 (and_2_out, not_1_out, priority_encoder_1_out[1]);
  and and_3 (and_3_out, priority_encoder_1_out[1], priority_encoder_1_out[0]);
  and and_4 (and_4_out, priority_encoder_1_out[1], not_3_out);
  and and_5 (and_5_out, not_2_out, priority_encoder_1_out[0]);
  and and_6 (and_6_out, priority_encoder_1_out[2], priority_encoder_1_out[0]);
  and and_7 (and_7_out, not_1_out, priority_encoder_1_out[1], not_3_out);
  or or_1 (or_1_out, and_1_out, and_2_out, priority_encoder_1_out[0]);
  or S2 (S2_out, and_1_out, and_3_out);
  or S3 (S3_out, priority_encoder_1_out[2], and_5_out, and_4_out);
  or S4 (S4_out, not_4_out, priority_encoder_1_out[1]);
  or S5 (S5_out, and_6_out, and_5_out);
  or S6 (S6_out, and_1_out, and_6_out, and_5_out, and_7_out);
  or S7 (S7_out, priority_encoder_1_out[2], priority_encoder_1_out[1], not_5_out);
  _7_Segment_Display u_7_segment_display_1 (
    .g(or_1_out), .f(S2_out), .a(S3_out), .b(S4_out), .e(S5_out), .d(S6_out), .c(S7_out));  // open: dp

  // Notes on the sheet:
  //   Button1
  //   Button 2
  //   Button 3
  //   Button 4
  //   Button 5
  //   Button 6
  //   Button 7
  //   Button 8
  //   E0E1-
  //   E0-E1
  //   E1E2
  //   E1E2-
  //   E1-E2
  //   E0E2
  //   E0-E1E2-
  //   S1
endmodule
