// Logisim project subtask_one_cylrx.circ as structural Verilog: 1 circuit, main circuit main
module main (
);

  wire button_1_out, button_2_out, button_3_out, button_4_out, button_5_out, button_6_out, button_7_out,
       button_8_out;
  wire [2:0] priority_encoder_1_out;

  Button button_1 (.out(button_1_out));
  Button button_2 (.out(button_2_out));
  Button button_3 (.out(button_3_out));
  Button button_4 (.out(button_4_out));
  Button button_5 (.out(button_5_out));
  Button button_6 (.out(button_6_out));
  Button button_7 (.out(button_7_out));
  Button button_8 (.out(button_8_out));
  Priority_Encoder priority_encoder_1 (
    .in0(button_1_out), .in1(button_2_out), .in2(button_3_out), .in3(button_4_out), .in4(button_5_out),
    .in5(button_6_out), .in6(button_7_out), .in7(button_8_out), .out(priority_encoder_1_out));  // open: en_in, gs, en_out
  LED led_1 (.in(priority_encoder_1_out[0]));
  LED led_2 (.in(priority_encoder_1_out[1]));
  LED led_3 (.in(priority_encoder_1_out[2]));
endmodule
