// Logisim project subtask_two_cylrx.circ as structural Verilog: 1 circuit, main circuit main
module main (
  input  in_1,
  input  in_2,
  input  in_3
);

  wire and_1_out, and_2_out, and_3_out, and_4_out, and_5_out, and_6_out, and_7_out, not_1_out, not_2_out,
       not_3_out, not_4_out, not_5_out, or_1_out, S2_out, S3_out, S4_out, S5_out, S6_out, S7_out;

  not not_1 (not_1_out, in_1);
  not not_2 (not_2_out, in_2);
  not not_3 (not_3_out, in_3);
  not not_4 (not_4_out, in_1);
  not not_5 (not_5_out, in_3);
  and and_1 (and_1_out, in_1, not_2_out);
  and and_2 (and_2_out, not_1_out, in_2);
  and and_3 (and_3_out, in_2, in_3);
  and and_4 (and_4_out, in_2, not_3_out);
  and and_5 (and_5_out, not_2_out, in_3);
  and and_6 (and_6_out, in_1, in_3);
  and and_7 (and_7_out, not_1_out, in_2, not_3_out);
  or or_1 (or_1_out, and_1_out, and_2_out, in_3);
  or S2 (S2_out, and_1_out, and_3_out);
  or S3 (S3_out, in_1, and_5_out, and_4_out);
  or S4 (S4_out, not_4_out, in_2);
  or S5 (S5_out, and_6_out, and_5_out);
  or S6 (S6_out, and_1_out, and_6_out, and_5_out, and_7_out);
  or S7 (S7_out, in_1, in_2, not_5_out);
  _7_Segment_Display u_7_segment_display_1 (
    .g(or_1_out), .f(S2_out), .a(S3_out), .b(S4_out), .e(S5_out), .d(S6_out), .c(S7_out));  // open: dp

  // Notes on the sheet:
  //   E0E1-
  //   E0-E1
  //   E1E2
  //   E1E2-
  //   E1-E2
  //   E0E2
  //   E0-E1E2-
  //   S1
endmodule
